# Fritzing sketch smart-compass-v2 (saved by Fritzing 0.9.3b)
circuit board: 8.31458cm x 6.52339cm
breadboards: 1

parts:
  Sensor = Adafruit LSM9DS1 9DoF Breakout [part_number="Adafruit #3387"]
  SD = Adafruit MicroSD card breakout board [part_number="Adafruit #254"]
  Feather_m0_RFM9x_Lora_Radio = Adafruit Feather M0 RFM9x LoRa [part_number="Adafruit #3178 or #3179"]
  Neopixel_D_G_V = Header 3 [package=screwterminal-3.5mm-3_lock.007s]
  GPS = Adafruit GPS FeatherWing [part_number="Adafruit #3133"]

nets:
  N1: Sensor.SDO_M, Sensor.SDO_AG, SD.DO, Feather_m0_RFM9x_Lora_Radio.MISO
  N2: Sensor.CS_MAG, Feather_m0_RFM9x_Lora_Radio.A3
  N3: Sensor.SDA, SD.DI, Feather_m0_RFM9x_Lora_Radio.MOSI
  N4: Sensor.SCL, SD.CLK, Feather_m0_RFM9x_Lora_Radio.SCK
  GND: Sensor.GND, SD.GND, Feather_m0_RFM9x_Lora_Radio.GND, Neopixel_D_G_V.2, GPS.GND
  +3V3: Sensor.VIN, SD.+3V3, Feather_m0_RFM9x_Lora_Radio.+3V3, Neopixel_D_G_V.3, GPS.3V
  N5: SD.CS, Feather_m0_RFM9x_Lora_Radio.A5
  N6: Feather_m0_RFM9x_Lora_Radio.D1, GPS.TX
  N7: Feather_m0_RFM9x_Lora_Radio.D0, GPS.RX
  N8: Feather_m0_RFM9x_Lora_Radio.A1, Neopixel_D_G_V.1

custom parts:
  Adafruit LSM9DS1 9DoF Breakout: Add motion, direction and orientation sensing to your Arduino project with this all-in-one 9-DOF sensor. Inside the chip are three sensors, one is a classic 3-axis accelerometer, which can tell you which direction is down towards the Earth (by measuring gravity) or how fast the board is accelerating in 3D space. The other is a 3-axis magnetometer that can sense where the strongest magnetic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
  Adafruit MicroSD card breakout board: Not just a simple breakout board, this microSD adapter goes the extra mile - designed for ease of use. Onboard 5v->3v regulator provides 150mA for power-hungry cards 3v level shifting means you can use this with ease on either 3v or 5v systems Uses a proper level shifting chip, not resistors: less problems, and faster read/write access Use 3 or 4 digital pins to read and write 2Gb+ of storage!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
  Adafruit Feather M0 RFM9x LoRa: This is the Adafruit Feather M0 RFM95 LoRa Radio - our take on an microcontroller with a "Long Range (LoRa)" packet radio transceiver with built in USB and battery charging. Its an Adafruit Feather M0 with a 433Mhz or 900MHz radio module cooked in! Great for making wireless networks that are more flexible than Bluetooth LE and without the high power requirements of WiFi. We have other boards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
  Adafruit GPS FeatherWing: Give your Feather a sense of place, with an Ultimate GPS FeatherWing. In 2013 we designed the Ultimate GPS module to satisfy all your GPS desires - and now we have brought its power and versatility plus more to our Feather series with the Adafruit Ultimate GPS FeatherWing! This FeatherWing plugs right into your Feather board and gives it a precise, sensitive, and low power GPS module for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

// code stored in the sketch: smart-compass.ino
// TODO: use addmod8

// TODO: how is clang-format deciding to order these? they aren't alphabetical
#include <AP_Declination.h>
#include <Adafruit_GPS.h>
#include <Adafruit_LSM9DS1.h>
#include <Adafruit_Sensor.h>
#include <ArduinoSort.h>
#include <Bounce2.h>
#include <FastLED.h>
#include <IniFile.h>
#include <RH_RF95.h>
#include <SD.h>
#include <SPI.h>
#include <elapsedMillis.h>
#include <pb_decode.h>
#include <pb_encode.h>
// TODO: fork TimeLib to include ms
#include <TimeLib.h>
#include <Wire.h>

#include "smart-compass.pb.h"

// Pins 0 and 1 are used for Serial1 (GPS)
#define RFM95_INT 3 // already wired for us
#define RFM95_RST 4 // already wired for us
#define LED_DATA_PIN 5
#define RFM95_CS 8 // already wired for us
#define VBAT_PIN 9 // already wired for us  // A7
#define SDCARD_CS_PIN 10  // TODO: moved to a different pin for cleaner traces
#define LSM9DS1_CSAG 11  // TODO: moved to a different pin for cleaner traces
#define LSM9DS1_CSM 12  // TODO: moved to a different pin for cleaner traces
#define RED_LED_PIN 13  // already wired for us
#define SPI_MISO_PIN 22 // shared between Radio+Sensors+SD
#define SPI_MOSI_PIN 23 // shared between Radio+Sensors+SD
#define SPI_SCK_PIN 24  // shared between Radio+Sensors+SD
#define gpsSerial Serial1

#define LED_CHIPSET NEOPIXEL

/* these variables are used by multiple ino files and I'm not sure the right place to put them */
// TODO: maybe pass these around as arguments instead of having them be global?

// lights for compass ring
const int num_LEDs = 16;
CRGB leds[num_LEDs];

// rotating "base color" used by some patterns
uint8_t g_hue = 0;

// the more peers, the longer it takes for peer data to update
const int max_peers = 4;

// setup messages for all possible peers
SmartCompassMessage compass_messages[max_peers] = {SmartCompassMessage_init_default};

// these are set by config
int my_network_id, my_peer_id, my_hue, my_saturation, num_peers;

// these are set by config or fallback to defaults
// TODO: making this unsigned makes IniConfig sad. they shouldn't ever be negative though!
int broadcast_time_ms, default_brightness, flashlight_density, frames_per_second, gps_update_s, max_peer_distance, ms_per_light_pattern,
  peer_led_ms, radio_power;

int time_zone_offset;

// offset between true and magnetic north
float magnetic_declination = 0.0;

// connect to the GPS
Adafruit_GPS GPS(&gpsSerial);

// save GPS data to SD card
String gps_log_filename = ""; // this is filled in during setupSD
File gps_log_file;

// keep us from transmitting too often
long last_transmitted[max_peers] = {0};

// TODO: this will probably change when I move from the breadboard to the PCB. give them better names (portrait, landscape?)
enum Orientation: byte {
  ORIENTED_UP, ORIENTED_DOWN, ORIENTED_USB_UP, ORIENTED_USB_DOWN, ORIENTED_PORTRAIT_UPSIDE_DOWN, ORIENTED_PORTRAIT
};

bool sd_setup, sensor_setup = false;

void setupSPI() {
  // https://github.com/ImprobableStudios/Feather_TFT_LoRa_Sniffer/blob/9a8012ba316a652da669fe097c4b76c98bbaf35c/Feather_TFT_LoRa_Sniffer.ino#L222
  // The RFM95 has a pulldown on this pin, so the radio
  // is technically always selected unless you set the pin low.
  // this will cause other SPI devices to fail to function as
  // expected because CS (active-low) will be selected for
  // the RFM95 at the same time.
  digitalWrite(RFM95_CS, HIGH);

  digitalWrite(SDCARD_CS_PIN, HIGH);

  digitalWrite(LSM9DS1_CSM, HIGH);
  digitalWrite(LSM9DS1_CSAG, HIGH);

  // TODO: configure SPI pins?

  delay(100); // give everything time to wake up

  SPI.begin();
}

void setup() {
  Serial.begin(115200);

  //delay(1000);
  while (!Serial) {
    ; // wait for serial port to connect. Needed for native USB
  }

  Serial.println("Setting up...");

  // Configure SPI pins for everything BEFORE trying to do anything with them individually
  setupSPI();

  randomSeed(analogRead(6));

  // configuration depends on SD card so do it first
  setupSD();

  setupConfig();

  // do more setup now that we have our configuration
  setupGPS();
  setupRadio();
  setupSensor();
  setupLights();

  // configure the timer to run at <sampleRate>Hertz
  tcConfigure(100);
  tcStartCounter();

  Serial.println("Starting...");
}

void loop() {
  // TODO: num_peers * num_peers can get pretty big!
  // each peer needs enough time to broadcast data for every other peer
  static unsigned int time_segments = num_peers * num_peers;
  static unsigned int time_segment_id, broadcasting_peer_id, broadcasted_peer_id;

  gpsReceive();

  updateLights();

  // TODO: fastled EVERY_N_SECONDS helper doesn't work for us. maybe if we passed variables

  if (timeStatus() == timeNotSet) {
    // TODO: set time from peer?
    //radioReceive();
  } else {
    // if it's our time to transmit, radioTransmit(), else wait for radioReceive()
    // TODO: should there be downtime when no one is transmitting or receiving?

    time_segment_id = (nowMillis() / broadcast_time_ms) % time_segments;
    broadcasting_peer_id = time_segment_id / num_peers;
    broadcasted_peer_id = time_segment_id % num_peers;

    if (broadcasting_peer_id == my_peer_id) {
      radioTransmit(broadcasted_peer_id);  // this will noop if we have transmitted recently
    } else {
      // TODO: have known down time so we can sleep longer?
      radioReceive();
    }
  }

  // don't sleep too long or you get in the way of radios. keep this less < framerate
  //delayToDither(10);
  FastLED.delay(10);
}
